// Logisim project MEM8B.circ as structural Verilog: 1 circuit, main circuit memoria
module memoria (
  input  I0,
  input  I1,
  input  I2,
  input  I3,
  input  A3,
  input  A2,
  input  A1,
  input  A0,
  input  CS,
  input  RD,
  input  OE,
  output O3,
  output O2,
  output O1,
  output O0
);

  wire and_1_out, and_2_out, and_3_out, and_4_out, and_5_out, and_6_out, and_7_out, and_8_out, and_9_out,
       and_10_out, and_11_out, and_12_out, and_13_out, and_14_out, and_15_out, and_16_out, and_17_out,
       and_18_out, and_19_out, and_20_out, and_21_out, and_22_out, and_23_out, and_24_out, and_25_out,
       and_26_out, and_27_out, and_28_out, and_29_out, and_30_out, and_31_out, and_32_out, and_33_out,
       and_34_out, and_35_out, and_36_out, and_37_out, and_38_out, and_39_out, and_40_out, and_41_out,
       and_42_out, and_43_out, and_44_out, and_45_out, and_46_out, and_47_out, and_48_out, and_49_out,
       and_50_out, and_51_out, and_52_out, and_53_out, and_54_out, and_55_out, and_56_out, and_57_out,
       and_58_out, and_59_out, and_60_out, and_61_out, and_62_out, and_63_out, and_64_out, and_65_out,
       and_66_out, and_67_out, and_68_out, and_69_out, and_70_out, and_71_out, and_72_out, and_73_out,
       and_74_out, and_75_out, and_76_out, and_77_out, and_78_out, and_79_out, and_80_out, and_81_out,
       and_82_out, and_83_out, and_84_out, and_85_out, and_86_out, and_87_out, and_88_out, and_89_out,
       and_90_out, and_91_out, and_92_out, and_93_out, and_94_out, and_95_out, and_96_out, and_97_out,
       and_99_out, not_1_out, not_2_out, not_3_out, not_4_out, not_5_out, not_6_out, not_7_out, not_8_out,
       not_9_out, not_10_out, not_11_out, not_12_out, not_13_out, not_14_out, not_15_out, not_16_out,
       not_17_out, not_18_out, not_19_out, not_20_out, not_21_out, not_22_out, not_23_out, not_24_out,
       not_25_out, not_26_out, not_27_out, not_28_out, not_29_out, not_30_out, not_31_out, not_32_out,
       not_33_out, not_34_out, or_1_out, or_2_out, or_3_out, or_4_out, undriven, W1_0_q, W1_1_q, W1_2_q,
       W1_3_q, W2_0_q, W2_1_q, W2_2_q, W2_3_q, W3_0_q, W3_1_q, W3_2_q, W3_3_q, W4_0_q, W4_1_q, W4_2_q,
       W4_3_q, W5_0_q, W5_1_q, W5_2_q, W5_3_q, W6_0_q, W6_1_q, W6_2_q, W6_3_q, W7_0_q, W7_1_q, W7_2_q,
       W7_3_q, W8_0_q, W8_1_q, W8_2_q, W8_3_q, W9_0_q, W9_1_q, W9_2_q, W9_3_q, W10_0_q, W10_1_q, W10_2_q,
       W10_3_q, W11_0_q, W11_1_q, W11_2_q, W11_3_q, W12_0_q, W12_1_q, W12_2_q, W12_3_q, W13_0_q, W13_1_q,
       W13_2_q, W13_3_q, W14_0_q, W14_1_q, W14_2_q, W14_3_q, W15_0_q, W15_1_q, W15_2_q, W15_3_q, W16_0_q,
       W16_1_q, W16_2_q, W16_3_q;

  not not_1 (not_1_out, A3);
  not not_2 (not_2_out, A2);
  not not_3 (not_3_out, A1);
  not not_4 (not_4_out, A0);
  not not_5 (not_5_out, A3);
  not not_6 (not_6_out, A2);
  not not_7 (not_7_out, A1);
  not not_8 (not_8_out, A3);
  not not_9 (not_9_out, A2);
  not not_10 (not_10_out, A0);
  not not_11 (not_11_out, A3);
  not not_12 (not_12_out, A2);
  not not_13 (not_13_out, A3);
  not not_14 (not_14_out, A1);
  not not_15 (not_15_out, A0);
  not not_16 (not_16_out, A3);
  not not_17 (not_17_out, A1);
  not not_18 (not_18_out, A3);
  not not_19 (not_19_out, A0);
  not not_20 (not_20_out, A3);
  not not_21 (not_21_out, A2);
  not not_22 (not_22_out, A1);
  not not_23 (not_23_out, A0);
  not not_24 (not_24_out, A2);
  not not_25 (not_25_out, A1);
  not not_26 (not_26_out, A2);
  not not_27 (not_27_out, A0);
  not not_28 (not_28_out, A2);
  not not_29 (not_29_out, A1);
  not not_30 (not_30_out, A0);
  not not_31 (not_31_out, A1);
  not not_32 (not_32_out, A0);
  not not_33 (not_33_out, A0);
  and and_1 (and_1_out, not_1_out, not_2_out, not_3_out, not_4_out);
  and and_2 (and_2_out, not_5_out, not_6_out, not_7_out, A0);
  and and_3 (and_3_out, not_8_out, not_9_out, A1, not_10_out);
  and and_4 (and_4_out, not_11_out, not_12_out, A1, A0);
  and and_5 (and_5_out, not_13_out, A2, not_14_out, not_15_out);
  and and_6 (and_6_out, not_16_out, A2, not_17_out, A0);
  and and_7 (and_7_out, not_18_out, A2, A1, not_19_out);
  and and_8 (and_8_out, not_20_out, A2, A1, A0);
  and and_9 (and_9_out, A3, not_21_out, not_22_out, not_23_out);
  and and_10 (and_10_out, A3, not_24_out, not_25_out, A0);
  and and_11 (and_11_out, A3, not_26_out, A1, not_27_out);
  and and_12 (and_12_out, A3, not_28_out, A1, A0);
  and and_13 (and_13_out, A3, A2, not_29_out, not_30_out);
  and and_14 (and_14_out, A3, A2, not_31_out, A0);
  and and_15 (and_15_out, A3, A2, A1, not_32_out);
  and and_16 (and_16_out, A3, A2, A1, not_33_out);
  and and_17 (and_17_out, CS, not_34_out);
  not not_34 (not_34_out, RD);
  and and_18 (and_18_out, and_17_out, and_1_out);
  and and_19 (and_19_out, and_17_out, and_2_out);
  and and_20 (and_20_out, and_17_out, and_3_out);
  and and_21 (and_21_out, and_17_out, and_4_out);
  and and_22 (and_22_out, and_17_out, and_5_out);
  and and_23 (and_23_out, and_17_out, and_6_out);
  and and_24 (and_24_out, and_17_out, and_7_out);
  and and_25 (and_25_out, and_17_out, and_8_out);
  and and_26 (and_26_out, and_17_out, and_9_out);
  and and_27 (and_27_out, and_17_out, and_10_out);
  and and_28 (and_28_out, and_17_out, and_11_out);
  and and_29 (and_29_out, and_17_out, and_12_out);
  and and_30 (and_30_out, and_17_out, and_13_out);
  and and_31 (and_31_out, and_17_out, and_14_out);
  and and_32 (and_32_out, and_17_out, and_15_out);
  and and_33 (and_33_out, and_17_out, and_16_out);
  and and_34 (and_34_out, RD, CS, OE);
  D_Flip_Flop W1_3 (.clk(and_18_out), .D(I3), .Q(W1_3_q));  // open: Qn, preset, en, reset
  D_Flip_Flop W2_3 (.clk(and_19_out), .D(I3), .Q(W2_3_q));  // open: Qn, preset, en, reset
  D_Flip_Flop W3_3 (.clk(and_20_out), .D(I3), .Q(W3_3_q));  // open: Qn, preset, en, reset
  D_Flip_Flop W4_3 (.clk(and_21_out), .D(I3), .Q(W4_3_q));  // open: Qn, preset, en, reset
  D_Flip_Flop W5_3 (.clk(and_22_out), .D(I3), .Q(W5_3_q));  // open: Qn, preset, en, reset
  D_Flip_Flop W6_3 (.clk(and_23_out), .D(I3), .Q(W6_3_q));  // open: Qn, preset, en, reset
  D_Flip_Flop W7_3 (.clk(and_24_out), .D(I3), .Q(W7_3_q));  // open: Qn, preset, en, reset
  D_Flip_Flop W8_3 (.clk(and_25_out), .D(I3), .Q(W8_3_q));  // open: Qn, preset, en, reset
  D_Flip_Flop W9_3 (.clk(and_26_out), .D(I3), .Q(W9_3_q));  // open: Qn, preset, en, reset
  D_Flip_Flop W10_3 (.clk(and_27_out), .D(I3), .Q(W10_3_q));  // open: Qn, preset, en, reset
  D_Flip_Flop W11_3 (.clk(and_28_out), .D(I3), .Q(W11_3_q));  // open: Qn, preset, en, reset
  D_Flip_Flop W12_3 (.clk(and_29_out), .D(I3), .Q(W12_3_q));  // open: Qn, preset, en, reset
  D_Flip_Flop W13_3 (.clk(and_30_out), .D(I3), .Q(W13_3_q));  // open: Qn, preset, en, reset
  D_Flip_Flop W14_3 (.clk(and_31_out), .D(I3), .Q(W14_3_q));  // open: Qn, preset, en, reset
  and and_35 (and_35_out, and_14_out, W14_3_q);
  D_Flip_Flop W15_3 (.clk(and_32_out), .D(I3), .Q(W15_3_q));  // open: Qn, preset, en, reset
  and and_36 (and_36_out, and_15_out, W15_3_q);
  D_Flip_Flop W16_3 (.clk(and_33_out), .D(I3), .Q(W16_3_q));  // open: Qn, preset, en, reset
  and and_37 (and_37_out, and_16_out, W16_3_q);
  and and_38 (and_38_out, and_10_out, W10_3_q);
  and and_39 (and_39_out, and_11_out, W11_3_q);
  and and_40 (and_40_out, and_12_out, W12_3_q);
  and and_41 (and_41_out, and_13_out, W13_3_q);
  and and_42 (and_42_out, and_6_out, W6_3_q);
  and and_43 (and_43_out, and_7_out, W7_3_q);
  and and_44 (and_44_out, and_8_out, W8_3_q);
  and and_45 (and_45_out, and_9_out, W9_3_q);
  or or_1 (or_1_out, and_37_out, and_36_out, and_35_out, and_41_out, and_40_out, and_39_out, and_38_out, and_45_out, and_44_out, and_43_out, and_42_out, and_49_out, and_48_out, and_47_out, and_46_out, and_50_out);
  and and_46 (and_46_out, and_2_out, W2_3_q);
  and and_47 (and_47_out, and_3_out, W3_3_q);
  and and_48 (and_48_out, and_4_out, W4_3_q);
  and and_49 (and_49_out, and_5_out, W5_3_q);
  and and_50 (and_50_out, and_1_out, W1_3_q);
  D_Flip_Flop W1_2 (.clk(and_18_out), .D(I2), .Q(W1_2_q));  // open: Qn, preset, en, reset
  D_Flip_Flop W2_2 (.clk(and_19_out), .D(I2), .Q(W2_2_q));  // open: Qn, preset, en, reset
  D_Flip_Flop W3_2 (.clk(and_20_out), .D(I2), .Q(W3_2_q));  // open: Qn, preset, en, reset
  D_Flip_Flop W4_2 (.clk(and_21_out), .D(I2), .Q(W4_2_q));  // open: Qn, preset, en, reset
  D_Flip_Flop W5_2 (.clk(and_22_out), .D(I2), .Q(W5_2_q));  // open: Qn, preset, en, reset
  D_Flip_Flop W6_2 (.clk(and_23_out), .D(I2), .Q(W6_2_q));  // open: Qn, preset, en, reset
  D_Flip_Flop W7_2 (.clk(and_24_out), .D(I2), .Q(W7_2_q));  // open: Qn, preset, en, reset
  D_Flip_Flop W8_2 (.clk(and_25_out), .D(I2), .Q(W8_2_q));  // open: Qn, preset, en, reset
  D_Flip_Flop W9_2 (.clk(and_26_out), .D(I2), .Q(W9_2_q));  // open: Qn, preset, en, reset
  D_Flip_Flop W10_2 (.clk(and_27_out), .D(I2), .Q(W10_2_q));  // open: Qn, preset, en, reset
  D_Flip_Flop W11_2 (.clk(and_28_out), .D(I2), .Q(W11_2_q));  // open: Qn, preset, en, reset
  D_Flip_Flop W12_2 (.clk(and_29_out), .D(I2), .Q(W12_2_q));  // open: Qn, preset, en, reset
  D_Flip_Flop W13_2 (.clk(and_30_out), .D(I2), .Q(W13_2_q));  // open: Qn, preset, en, reset
  D_Flip_Flop W14_2 (.clk(and_31_out), .D(I2), .Q(W14_2_q));  // open: Qn, preset, en, reset
  and and_51 (and_51_out, and_14_out, W14_2_q);
  D_Flip_Flop W15_2 (.clk(and_32_out), .D(I2), .Q(W15_2_q));  // open: Qn, preset, en, reset
  and and_52 (and_52_out, and_15_out, W15_2_q);
  D_Flip_Flop W16_2 (.clk(and_33_out), .D(I2), .Q(W16_2_q));  // open: Qn, preset, en, reset
  and and_53 (and_53_out, and_16_out, W16_2_q);
  and and_54 (and_54_out, and_10_out, W10_2_q);
  and and_55 (and_55_out, and_11_out, W11_2_q);
  and and_56 (and_56_out, and_12_out, W12_2_q);
  and and_57 (and_57_out, and_13_out, W13_2_q);
  and and_58 (and_58_out, and_6_out, W6_2_q);
  and and_59 (and_59_out, and_7_out, W7_2_q);
  and and_60 (and_60_out, and_8_out, W8_2_q);
  and and_61 (and_61_out, and_9_out, W9_2_q);
  or or_2 (or_2_out, and_53_out, and_52_out, and_51_out, and_57_out, and_56_out, and_55_out, and_54_out, and_61_out, and_60_out, and_59_out, and_58_out, and_65_out, and_64_out, and_63_out, and_62_out, and_66_out);
  and and_62 (and_62_out, and_2_out, W2_2_q);
  and and_63 (and_63_out, and_3_out, W3_2_q);
  and and_64 (and_64_out, and_4_out, W4_2_q);
  and and_65 (and_65_out, and_5_out, W5_2_q);
  and and_66 (and_66_out, and_1_out, W1_2_q);
  D_Flip_Flop W1_1 (.clk(and_18_out), .D(I1), .Q(W1_1_q));  // open: Qn, preset, en, reset
  D_Flip_Flop W2_1 (.clk(and_19_out), .D(I1), .Q(W2_1_q));  // open: Qn, preset, en, reset
  D_Flip_Flop W3_1 (.clk(and_20_out), .D(I1), .Q(W3_1_q));  // open: Qn, preset, en, reset
  D_Flip_Flop W4_1 (.clk(and_21_out), .D(I1), .Q(W4_1_q));  // open: Qn, preset, en, reset
  D_Flip_Flop W5_1 (.clk(and_22_out), .D(I1), .Q(W5_1_q));  // open: Qn, preset, en, reset
  D_Flip_Flop W6_1 (.clk(and_23_out), .D(I1), .Q(W6_1_q));  // open: Qn, preset, en, reset
  D_Flip_Flop W7_1 (.clk(and_24_out), .D(I1), .Q(W7_1_q));  // open: Qn, preset, en, reset
  D_Flip_Flop W8_1 (.clk(and_25_out), .D(I1), .Q(W8_1_q));  // open: Qn, preset, en, reset
  D_Flip_Flop W9_1 (.clk(and_26_out), .D(I1), .Q(W9_1_q));  // open: Qn, preset, en, reset
  D_Flip_Flop W10_1 (.clk(and_27_out), .D(I1), .Q(W10_1_q));  // open: Qn, preset, en, reset
  D_Flip_Flop W11_1 (.clk(and_28_out), .D(I1), .Q(W11_1_q));  // open: Qn, preset, en, reset
  D_Flip_Flop W12_1 (.clk(and_29_out), .D(I1), .Q(W12_1_q));  // open: Qn, preset, en, reset
  D_Flip_Flop W13_1 (.clk(and_30_out), .D(I1), .Q(W13_1_q));  // open: Qn, preset, en, reset
  D_Flip_Flop W14_1 (.clk(and_31_out), .D(I1), .Q(W14_1_q));  // open: Qn, preset, en, reset
  and and_67 (and_67_out, and_14_out, W14_1_q);
  D_Flip_Flop W15_1 (.clk(and_32_out), .D(I1), .Q(W15_1_q));  // open: Qn, preset, en, reset
  and and_68 (and_68_out, and_15_out, W15_1_q);
  D_Flip_Flop W16_1 (.clk(and_33_out), .D(I1), .Q(W16_1_q));  // open: Qn, preset, en, reset
  and and_69 (and_69_out, and_16_out, W16_1_q);
  and and_70 (and_70_out, and_10_out, W10_1_q);
  and and_71 (and_71_out, and_11_out, W11_1_q);
  and and_72 (and_72_out, and_12_out, W12_1_q);
  and and_73 (and_73_out, and_13_out, W13_1_q);
  and and_74 (and_74_out, and_6_out, W6_1_q);
  and and_75 (and_75_out, and_7_out, W7_1_q);
  and and_76 (and_76_out, and_8_out, W8_1_q);
  and and_77 (and_77_out, and_9_out, W9_1_q);
  or or_3 (or_3_out, and_69_out, and_68_out, and_67_out, and_73_out, and_72_out, and_71_out, and_70_out, and_77_out, and_76_out, and_75_out, and_74_out, and_81_out, and_80_out, and_79_out, and_78_out, and_82_out);
  and and_78 (and_78_out, and_2_out, W2_1_q);
  and and_79 (and_79_out, and_3_out, W3_1_q);
  and and_80 (and_80_out, and_4_out, W4_1_q);
  and and_81 (and_81_out, and_5_out, W5_1_q);
  and and_82 (and_82_out, and_1_out, W1_1_q);
  D_Flip_Flop W1_0 (.clk(and_18_out), .D(I0), .Q(W1_0_q));  // open: Qn, preset, en, reset
  D_Flip_Flop W2_0 (.clk(and_19_out), .D(I0), .Q(W2_0_q));  // open: Qn, preset, en, reset
  D_Flip_Flop W3_0 (.clk(and_20_out), .D(I0), .Q(W3_0_q));  // open: Qn, preset, en, reset
  D_Flip_Flop W4_0 (.clk(and_21_out), .D(I0), .Q(W4_0_q));  // open: Qn, preset, en, reset
  D_Flip_Flop W5_0 (.clk(and_22_out), .D(I0), .Q(W5_0_q), .en(undriven), .reset(undriven));  // open: Qn, preset
  D_Flip_Flop W6_0 (.clk(and_23_out), .D(I0), .Q(W6_0_q));  // open: Qn, preset, en, reset
  D_Flip_Flop W7_0 (.clk(and_24_out), .D(I0), .Q(W7_0_q));  // open: Qn, preset, en, reset
  D_Flip_Flop W8_0 (.clk(and_25_out), .D(I0), .Q(W8_0_q));  // open: Qn, preset, en, reset
  D_Flip_Flop W9_0 (.clk(and_26_out), .D(I0), .Q(W9_0_q));  // open: Qn, preset, en, reset
  D_Flip_Flop W10_0 (.clk(and_27_out), .D(I0), .Q(W10_0_q));  // open: Qn, preset, en, reset
  D_Flip_Flop W11_0 (.clk(and_28_out), .D(I0), .Q(W11_0_q));  // open: Qn, preset, en, reset
  D_Flip_Flop W12_0 (.clk(and_29_out), .D(I0), .Q(W12_0_q));  // open: Qn, preset, en, reset
  D_Flip_Flop W13_0 (.clk(and_30_out), .D(I0), .Q(W13_0_q));  // open: Qn, preset, en, reset
  D_Flip_Flop W14_0 (.clk(and_31_out), .D(I0), .Q(W14_0_q));  // open: Qn, preset, en, reset
  and and_83 (and_83_out, and_14_out, W14_0_q);
  D_Flip_Flop W15_0 (.clk(and_32_out), .D(I0), .Q(W15_0_q));  // open: Qn, preset, en, reset
  and and_84 (and_84_out, and_15_out, W15_0_q);
  D_Flip_Flop W16_0 (.clk(and_33_out), .D(I0), .Q(W16_0_q));  // open: Qn, preset, en, reset
  and and_85 (and_85_out, and_16_out, W16_0_q);
  and and_86 (and_86_out, and_10_out, W10_0_q);
  and and_87 (and_87_out, and_11_out, W11_0_q);
  and and_88 (and_88_out, and_12_out, W12_0_q);
  and and_89 (and_89_out, and_13_out, W13_0_q);
  and and_90 (and_90_out, and_6_out, W6_0_q);
  and and_91 (and_91_out, and_7_out, W7_0_q);
  and and_92 (and_92_out, and_8_out, W8_0_q);
  and and_93 (and_93_out, and_9_out, W9_0_q);
  or or_4 (or_4_out, and_85_out, and_84_out, and_83_out, and_89_out, and_88_out, and_87_out, and_86_out, and_93_out, and_92_out, and_91_out, and_90_out, and_97_out, and_96_out, and_95_out, and_94_out, and_99_out);
  and and_94 (and_94_out, and_2_out, W2_0_q);
  and and_95 (and_95_out, and_3_out, W3_0_q);
  and and_96 (and_96_out, and_4_out, W4_0_q);
  and and_97 (and_97_out, and_5_out, W5_0_q);
  // AND_Gate and_98 has open pins: in1=and_96_out, out=open
  and and_99 (and_99_out, and_1_out, W1_0_q);
  assign O3 = and_34_out ? or_4_out : 1'bz;  // Controlled_Buffer controlled_buffer_1
  assign O2 = and_34_out ? or_3_out : 1'bz;  // Controlled_Buffer controlled_buffer_2
  assign O1 = and_34_out ? or_2_out : 1'bz;  // Controlled_Buffer controlled_buffer_3
  assign O0 = and_34_out ? or_1_out : 1'bz;  // Controlled_Buffer controlled_buffer_4
endmodule
