// Logisim project TECL.circ as structural Verilog: 1 circuit, main circuit teclado
module teclado (
  input  _0,
  input  _1,
  input  _2,
  input  _3,
  input  _4,
  input  _5,
  input  _6,
  input  _7,
  input  _8,
  input  _9,
  input  GRAVAR,
  input  LER,
  input  POWER,
  output D0,
  output D1,
  output D2,
  output D3,
  output E3,
  output E2,
  output E1,
  output E0,
  output CS,
  output RD,
  output OE
);

  wire and_1_out, and_2_out, and_3_out, and_4_out, and_5_out, and_6_out, and_7_out, and_8_out, and_9_out,
       and_10_out, and_11_out, and_12_out, and_13_out, and_14_out, and_15_out, and_16_out, and_17_out,
       and_18_out, and_19_out, and_20_out, and_21_out, and_22_out, and_23_out, and_24_out, and_25_out,
       and_26_out, and_27_out, and_28_out, and_29_out, and_30_out, and_31_out, and_32_out, and_33_out,
       and_34_out, and_35_out, and_36_out, and_37_out, and_38_out, and_39_out, and_40_out, and_41_out,
       and_42_out, and_43_out, and_44_out, and_45_out, and_46_out, controlled_buffer_1_out,
       controlled_buffer_2_out, d_ff_1_q, d_ff_2_q, d_ff_3_q, d_ff_4_q, d_ff_5_q, d_ff_6_q, d_ff_7_q,
       d_ff_8_q, not_1_out, not_3_out, not_4_out, not_5_out, not_6_out, not_7_out, not_8_out, not_9_out,
       not_10_out, not_11_out, not_12_out, not_13_out, not_14_out, not_15_out, not_16_out, not_17_out,
       not_18_out, not_19_out, not_20_out, not_21_out, not_22_out, not_23_out, not_24_out, not_25_out,
       not_26_out, not_27_out, not_28_out, t_ff_1_q, xor_1_out, xor_2_out, xor_3_out, xor_4_out, xor_5_out,
       xor_6_out, xor_7_out, xor_8_out, xor_9_out;

  ExactlyOne xor_1 (
    .out(xor_1_out), .in0(_0), .in1(_1), .in2(_2), .in3(_3), .in4(_4), .in5(_5), .in6(_6), .in7(_7),
    .in8(_8), .in9(_9));
  not not_1 (not_1_out, GRAVAR);
  not not_2 (not_1_out, GRAVAR);
  and and_1 (and_1_out, not_1_out, GRAVAR);
  not not_3 (not_3_out, _0);
  not not_4 (not_4_out, _0);
  not not_5 (not_5_out, _0);
  not not_6 (not_6_out, _0);
  not not_7 (not_7_out, _1);
  not not_8 (not_8_out, _1);
  not not_9 (not_9_out, _1);
  not not_10 (not_10_out, _2);
  not not_11 (not_11_out, _2);
  not not_12 (not_12_out, _2);
  not not_13 (not_13_out, _3);
  not not_14 (not_14_out, _3);
  not not_15 (not_15_out, _4);
  not not_16 (not_16_out, _4);
  not not_17 (not_17_out, _4);
  not not_18 (not_18_out, _5);
  not not_19 (not_19_out, _5);
  not not_20 (not_20_out, _6);
  not not_21 (not_21_out, _6);
  not not_22 (not_22_out, _7);
  not not_23 (not_23_out, _8);
  not not_24 (not_24_out, _8);
  not not_25 (not_25_out, _8);
  not not_26 (not_26_out, _9);
  not not_27 (not_27_out, _9);
  and and_2 (and_2_out, not_1_out, GRAVAR);
  and and_3 (and_3_out, GRAVAR, GRAVAR);
  and and_4 (and_4_out, not_6_out, _0);
  and and_5 (and_5_out, not_5_out, _0);
  and and_6 (and_6_out, _1, _1);
  and and_7 (and_7_out, not_9_out, _1);
  and and_8 (and_8_out, not_12_out, _2);
  and and_9 (and_9_out, _2, _2);
  and and_10 (and_10_out, _3, _3);
  and and_11 (and_11_out, _3, _3);
  and and_12 (and_12_out, not_16_out, _4);
  and and_13 (and_13_out, not_17_out, _4);
  and and_14 (and_14_out, not_19_out, _5);
  and and_15 (and_15_out, _5, _5);
  and and_16 (and_16_out, not_21_out, _6);
  and and_17 (and_17_out, _6, _6);
  and and_18 (and_18_out, _7, _7);
  and and_19 (and_19_out, _7, _7);
  and and_20 (and_20_out, not_25_out, _8);
  and and_21 (and_21_out, not_24_out, _8);
  and and_22 (and_22_out, _9, _9);
  and and_23 (and_23_out, not_27_out, _9);
  T_Flip_Flop t_ff_1 (.clk(GRAVAR), .T(GRAVAR), .Q(t_ff_1_q));  // open: Qn, preset, reset, en
  xor xor_2 (xor_2_out, and_3_out, LER);
  xor xor_3 (xor_3_out, and_2_out, LER);
  xor xor_4 (xor_4_out, and_1_out, LER);
  xor xor_5 (xor_5_out, GRAVAR, LER);
  and and_24 (and_24_out, not_4_out, _0);
  and and_25 (and_25_out, not_3_out, _0);
  and and_26 (and_26_out, not_8_out, _1);
  and and_27 (and_27_out, not_7_out, _1);
  and and_28 (and_28_out, not_10_out, _2);
  and and_29 (and_29_out, not_11_out, _2);
  and and_30 (and_30_out, not_14_out, _3);
  and and_31 (and_31_out, not_13_out, _3);
  and and_32 (and_32_out, _4, _4);
  and and_33 (and_33_out, not_15_out, _4);
  and and_34 (and_34_out, not_18_out, _5);
  and and_35 (and_35_out, _5, _5);
  and and_36 (and_36_out, not_20_out, _6);
  and and_37 (and_37_out, _6, _6);
  and and_38 (and_38_out, _7, _7);
  and and_39 (and_39_out, not_22_out, _7);
  and and_40 (and_40_out, _8, _8);
  and and_41 (and_41_out, not_23_out, _8);
  and and_42 (and_42_out, not_26_out, _9);
  and and_43 (and_43_out, _9, _9);
  and and_44 (and_44_out, xor_1_out, t_ff_1_q);
  not not_28 (not_28_out, t_ff_1_q);
  and and_45 (and_45_out, not_28_out, xor_1_out);
  ExactlyOne xor_6 (
    .out(xor_6_out), .in0(and_22_out), .in1(and_20_out), .in2(and_19_out), .in3(and_16_out),
    .in4(and_15_out), .in5(and_13_out), .in6(and_11_out), .in7(and_8_out), .in8(and_6_out), .in9(and_4_out));
  assign controlled_buffer_1_out = POWER ? and_44_out : 1'bz;  // Controlled_Buffer controlled_buffer_1
  assign controlled_buffer_2_out = POWER ? and_45_out : 1'bz;  // Controlled_Buffer controlled_buffer_2
  D_Flip_Flop d_ff_1 (.clk(controlled_buffer_1_out), .D(xor_6_out), .Q(d_ff_1_q));  // open: Qn, preset, en, reset
  D_Flip_Flop d_ff_2 (.clk(controlled_buffer_2_out), .D(xor_6_out), .Q(d_ff_2_q));  // open: Qn, preset, en, reset
  ExactlyOne xor_7 (
    .out(xor_7_out), .in0(and_23_out), .in1(and_21_out), .in2(and_18_out), .in3(and_17_out),
    .in4(and_14_out), .in5(and_12_out), .in6(and_10_out), .in7(and_9_out), .in8(and_7_out), .in9(and_5_out));
  D_Flip_Flop d_ff_3 (.clk(controlled_buffer_1_out), .D(xor_7_out), .Q(d_ff_3_q));  // open: Qn, preset, en, reset
  D_Flip_Flop d_ff_4 (.clk(controlled_buffer_2_out), .D(xor_7_out), .Q(d_ff_4_q));  // open: Qn, preset, en, reset
  ExactlyOne xor_8 (
    .out(xor_8_out), .in0(and_42_out), .in1(and_41_out), .in2(and_38_out), .in3(and_37_out),
    .in4(and_35_out), .in5(and_32_out), .in6(and_30_out), .in7(and_29_out), .in8(and_26_out), .in9(and_24_out));
  D_Flip_Flop d_ff_5 (.clk(controlled_buffer_1_out), .D(xor_8_out), .Q(d_ff_5_q));  // open: Qn, preset, en, reset
  D_Flip_Flop d_ff_6 (.clk(controlled_buffer_2_out), .D(xor_8_out), .Q(d_ff_6_q));  // open: Qn, preset, en, reset
  ExactlyOne xor_9 (
    .out(xor_9_out), .in0(and_43_out), .in1(and_40_out), .in2(and_39_out), .in3(and_36_out),
    .in4(and_34_out), .in5(and_33_out), .in6(and_31_out), .in7(and_28_out), .in8(and_27_out), .in9(and_25_out));
  D_Flip_Flop d_ff_7 (.clk(controlled_buffer_1_out), .D(xor_9_out), .Q(d_ff_7_q));  // open: Qn, preset, en, reset
  D_Flip_Flop d_ff_8 (.clk(controlled_buffer_2_out), .D(xor_9_out), .Q(d_ff_8_q));  // open: Qn, preset, en, reset
  assign D0 = and_46_out ? d_ff_1_q : 1'bz;  // Controlled_Buffer controlled_buffer_3
  assign D1 = and_46_out ? d_ff_3_q : 1'bz;  // Controlled_Buffer controlled_buffer_4
  assign D2 = and_46_out ? d_ff_5_q : 1'bz;  // Controlled_Buffer controlled_buffer_5
  assign D3 = and_46_out ? d_ff_7_q : 1'bz;  // Controlled_Buffer controlled_buffer_6
  assign E3 = and_46_out ? d_ff_8_q : 1'bz;  // Controlled_Buffer controlled_buffer_7
  assign E2 = and_46_out ? d_ff_6_q : 1'bz;  // Controlled_Buffer controlled_buffer_8
  assign E1 = and_46_out ? d_ff_4_q : 1'bz;  // Controlled_Buffer controlled_buffer_9
  assign E0 = and_46_out ? d_ff_2_q : 1'bz;  // Controlled_Buffer controlled_buffer_10
  assign CS = and_46_out ? xor_2_out : 1'bz;  // Controlled_Buffer controlled_buffer_11
  assign RD = and_46_out ? xor_3_out : 1'bz;  // Controlled_Buffer controlled_buffer_12
  assign OE = and_46_out ? xor_4_out : 1'bz;  // Controlled_Buffer controlled_buffer_13
  and and_46 (and_46_out, xor_5_out, POWER);

  // Notes on the sheet:
  //   DADOS
  //   ENDEREÇO
endmodule
