// Logisim project TRABOP1.circ as structural Verilog: 1 circuit, main circuit main
module main (
  input  in_1
);

  wire _0_out, _1_out, _2_out, _3_out, _4_out, _5_out, _6_out, _7_out, _8_out, _9_out, GRAVAR_out, LER_out,
       teclado_1_cs, teclado_1_d0, teclado_1_d1, teclado_1_d2, teclado_1_d3, teclado_1_e0, teclado_1_e1,
       teclado_1_e2, teclado_1_e3, teclado_1_oe, teclado_1_rd;
  wire [3:0] memoria_1_o3;

  Button _0 (.out(_0_out));
  Button _1 (.out(_1_out));
  Button _2 (.out(_2_out));
  Button _3 (.out(_3_out));
  Button _4 (.out(_4_out));
  Button _5 (.out(_5_out));
  Button _6 (.out(_6_out));
  Button _7 (.out(_7_out));
  Button _8 (.out(_8_out));
  Button _9 (.out(_9_out));
  Button GRAVAR (.out(GRAVAR_out));
  Button LER (.out(LER_out));
  teclado teclado_1 (
    ._0(_0_out), ._1(_1_out), ._2(_2_out), ._3(_3_out), ._4(_4_out), ._5(_5_out), ._6(_6_out), ._7(_7_out),
    ._8(_8_out), ._9(_9_out), .GRAVAR(GRAVAR_out), .LER(LER_out), .POWER(in_1), .D0(teclado_1_d0),
    .D1(teclado_1_d1), .D2(teclado_1_d2), .D3(teclado_1_d3), .E3(teclado_1_e3), .E2(teclado_1_e2),
    .E1(teclado_1_e1), .E0(teclado_1_e0), .CS(teclado_1_cs), .RD(teclado_1_rd), .OE(teclado_1_oe));
  memoria memoria_1 (
    .I0(teclado_1_d0), .I1(teclado_1_d1), .I2(teclado_1_d2), .I3(teclado_1_d3), .A3(teclado_1_e3),
    .A2(teclado_1_e2), .A1(teclado_1_e1), .A0(teclado_1_e0), .CS(teclado_1_cs), .RD(teclado_1_rd),
    .OE(teclado_1_oe), .O3(memoria_1_o3[0]), .O2(memoria_1_o3[1]), .O1(memoria_1_o3[2]), .O0(memoria_1_o3[3]));
  Hex_Digit_Display hex_digit_display_1 (.value(memoria_1_o3));  // open: dp
endmodule
